# Fritzing sketch training-bike (saved by Fritzing 0.9.10b)
circuit board: 8.46667cm x 5.64444cm
breadboards: 1

parts:
  H_bridge = L293D [package=THT]
  Button_1 = Momentary Switch [package=tactile-pth]
  Button_2 = Momentary Switch [package=tactile-pth]
  VCC = Battery block 9V
  Motor = DC Motor [voltage_(max)=6V voltage_(min)=3V]
  R2 = Resistor [tolerance=±5% resistance=10k package=THT]
  R1 = Resistor [tolerance=±5% resistance=10k package=THT]
  Arduino = Arduino Micro (Rev3)

nets:
  N1: H_bridge.In_1, Arduino.D3/SCL
  N2: H_bridge.Out_1_(_Controlled_by_Enable_1_), Motor.pin_1
  N3: H_bridge.0V, VCC.-, R2.Pin_0, R1.Pin_0, Arduino.GND
  N4: H_bridge.Out_2_(_Controlled_by_Enable_1_), Motor.pin_2
  N5: H_bridge.In_2, Arduino.D2/SDA
  N6: H_bridge.+Vmotor, Button_1.1, Button_2.1, VCC.+, Arduino.5V
  N7: Button_1.2, Arduino.D5_PWM
  N8: Button_1.3, R2.Pin_1
  N9: Button_2.2, Arduino.D4_PWM/A6
  N10: Button_2.3, R1.Pin_1
